# Fritzing sketch _core (saved by Fritzing 0.9.6b)
breadboards: 1

parts:
  Mod1 = Raspberry Pi Pico
  PCM5102A_I2S_Stereo_DAC2 = PCM5102A I2S Stereo DAC
  Part2 = Adafruit SDIO microSD Breakout

nets:
  GND: Mod1.pin_2, PCM5102A_I2S_Stereo_DAC2.DEMP, PCM5102A_I2S_Stereo_DAC2.GND, Part2.GND
  N1: Mod1.pin_3, Mod1.pin_8, Mod1.pin_13, Mod1.pin_18, Mod1.pin_23, Mod1.pin_28, Mod1.pin_33, Mod1.pin_38
  N2: Mod1.pin_14, Part2.SCLK
  N3: Mod1.pin_15, Part2.DI
  N4: Mod1.pin_17, Part2.DAT1
  N5: Mod1.pin_19, Part2.DAT2
  N6: Mod1.pin_20, Part2.CS
  N7: Mod1.pin_21, PCM5102A_I2S_Stereo_DAC2.BCK
  N8: Mod1.pin_22, PCM5102A_I2S_Stereo_DAC2.LRCK
  N9: Mod1.pin_24, PCM5102A_I2S_Stereo_DAC2.DIN
  VIN: Mod1.pin_37, PCM5102A_I2S_Stereo_DAC2.FLT, PCM5102A_I2S_Stereo_DAC2.VIN, Part2.3.3V

custom parts:
  Raspberry Pi Pico: Raspberry Pi Pico. Based around the RP2040 microcontroller the Pico is a low cost microcontroller device bringing Raspberry Pi quality, cost, and easy of use to the microcontroller space. Jan 2021, Split part in to two versions: tht (this one) and SMD. This one will drill holes for a .1 in header in pcb to allow plugging in the module as well as providing pads to solder the module to the top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
