# Fritzing sketch zeptoboard (saved by Fritzing 0.9.6b)
breadboards: 1

parts:
  Mod2 = Raspberry Pi Pico
  Part3 = Adafruit SDIO microSD Breakout
  PCM5102A_I2S_Stereo_DAC3 = PCM5102A I2S Stereo DAC

nets:
  GND: Mod2.pin_3, Mod2.pin_8, Mod2.pin_13, Mod2.pin_18, Mod2.pin_23, Mod2.pin_28, Mod2.pin_33, Mod2.pin_38, Part3.GND, PCM5102A_I2S_Stereo_DAC3.SCK, PCM5102A_I2S_Stereo_DAC3.GND
  N1: Mod2.pin_14, Part3.SCLK
  N2: Mod2.pin_15, Part3.DI
  N3: Mod2.pin_16, Part3.DO
  N4: Mod2.pin_17, Part3.DAT1
  N5: Mod2.pin_19, Part3.DAT2
  N6: Mod2.pin_20, Part3.CS
  N7: Mod2.pin_21, PCM5102A_I2S_Stereo_DAC3.BCK
  N8: Mod2.pin_22, PCM5102A_I2S_Stereo_DAC3.LRCK
  N9: Mod2.pin_24, PCM5102A_I2S_Stereo_DAC3.DIN
  N10: Mod2.pin_37, Part3.3.3V
  N11: Mod2.pin_39, PCM5102A_I2S_Stereo_DAC3.VIN

custom parts:
  Raspberry Pi Pico: Raspberry Pi Pico. Based around the RP2040 microcontroller the Pico is a low cost microcontroller device bringing Raspberry Pi quality, cost, and easy of use to the microcontroller space. Jan 2021, Split part in to two versions: tht (this one) and SMD. This one will drill holes for a .1 in header in pcb to allow plugging in the module as well as providing pads to solder the module to the top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
